# Fritzing sketch Automated Window System Skectch (saved by Fritzing 0.9.10b)

parts:
  Part2 = MQ-4
  YL-83_-_Control_Board2 = YL-83 Rain Sensor - Control Board
  YL-83_-_Detection_Board2 = YL-83 Rain Sensor - Detection Board
  J3 = Piezo Speaker
  Onderdeel2 = Arduino Uno (Rev3)
  LCD2 = LCD screen
  LCM1602_IIC2 = LCM1602 IIC [part_number="LCM1602 IIC" chip_label="LCM1602 IIC" package="DIP (Dual Inline) [THT]"]
  DHT1 = DHT11 Humitidy and Temperature Sensor
  R2 = Resistor [tolerance=±5% resistance=10k package="0402 [SMD]"]
  Part3 = MQ-4
  PIR1 = PIR sensor
  Part4 = Infra red receiver
  D2F1 = D2F-FL Omron Snap Action Limit Switch with Level
  D2F2 = D2F-FL Omron Snap Action Limit Switch with Level
  R3 = Resistor [tolerance=±5% resistance=10k power=0.25 package=THT]
  R4 = Resistor [tolerance=±5% resistance=10k power=0.25 package=THT]
  Driver2 = 28BYJ-48 Driver Module [part_number=ULN2003 package=THT]
  SM2 = 28BYJ-48 Stepper Motor [part_number=28BYJ-48]
  Power_plug2 = Power plug
  Driver3 = 28BYJ-48 Driver Module [part_number=ULN2003 package=THT]
  SM3 = 28BYJ-48 Stepper Motor [part_number=28BYJ-48]
  Power_plug3 = Power plug
  SERVO1 = Tower Pro SG90 servo [part_number=101246]
  SERVO2 = Tower Pro SG90 servo [part_number=101246]
  MH-ET_LIVE_ESP32_DEVKIT1 = MH-ET LIVE ESP32 DEVKIT 38 pins
  LED1 = RGB LED (com. cathode, rbg) [package="5 mm [THT]"]
  R6 = Resistor [tolerance=±5% resistance=220 power=0.25 package=THT]
  R7 = Resistor [tolerance=±5% resistance=220 power=0.25 package=THT]
  R8 = Resistor [tolerance=±5% resistance=220 power=0.25 package=THT]
  C1 = Capacitor Polarized [package=panasonic_d]  # not connected
  R9 = Resistor [tolerance=±5% resistance=1.5k package="2512 [SMD]"]  # not connected
  C2 = Capacitor Polarized [package=panasonic_d]  # not connected
  R10 = Resistor [tolerance=±5% resistance=1.5k package="2512 [SMD]"]  # not connected
  S1 = Pushbutton [package=THT]
  HCF_1 = HCF 4067 [package="DIP24 [THT]"]  # not connected
  U2 = 74HC595 [package="DIP16 [THT]"]  # not connected
  HCF_2 = HCF 4067 [package="DIP24 [THT]"]  # not connected
  U1 = 74HC595 [package="DIP16 [THT]"]  # not connected

nets:
  N1: Part2.GND, Onderdeel2.A3
  N2: YL-83_-_Control_Board2.AO, Onderdeel2.A0
  N3: YL-83_-_Control_Board2.POS, YL-83_-_Detection_Board2.POS
  N4: YL-83_-_Control_Board2.NEG, YL-83_-_Detection_Board2.NEG
  N5: J3.pin2, Onderdeel2.D6_PWM
  N6: Onderdeel2.A2, Part3.GND
  N7: Onderdeel2.A4/SDA, LCM1602_IIC2.SDA
  N8: Onderdeel2.A5/SCL, LCM1602_IIC2.SCL
  N9: Onderdeel2.D8, R2.Pin_1
  N10: Onderdeel2.D9_PWM, R8.Pin_1
  N11: Onderdeel2.D10_PWM/SS, R7.Pin_1
  N12: Onderdeel2.D11_PWM/MOSI, R6.Pin_1
  N13: Onderdeel2.D12/MISO, SERVO1.+5V
  GND: Onderdeel2.GND, LCM1602_IIC2.GND
  N14: Onderdeel2.D0/RX, MH-ET_LIVE_ESP32_DEVKIT1.TXD0
  N15: Onderdeel2.D1/TX, MH-ET_LIVE_ESP32_DEVKIT1.RXD0
  N16: Onderdeel2.D2, R4.Pin_1
  N17: Onderdeel2.D3_PWM, R3.Pin_1
  N18: Onderdeel2.D4, PIR1.SIG
  N19: Onderdeel2.D5_PWM, Part4.Data
  N20: Onderdeel2.D7, SERVO2.+5V
  N21: Onderdeel2.RESET, S1.leg0
  5V: Onderdeel2.5V, LCM1602_IIC2.VCC
  VSS: LCD2.VSS, LCM1602_IIC2.VSS
  VDD: LCD2.VDD, LCM1602_IIC2.VDD
  N22: LCD2.V0, LCM1602_IIC2.V0
  N23: LCD2.RS, LCM1602_IIC2.RS
  N24: LCD2.R/W, LCM1602_IIC2.RW
  N25: LCD2.E, LCM1602_IIC2.E
  N26: LCD2.DB0, LCM1602_IIC2.D0
  N27: LCD2.DB1, LCM1602_IIC2.D1
  N28: LCD2.DB2, LCM1602_IIC2.D2
  N29: LCD2.DB3, LCM1602_IIC2.D3
  N30: LCD2.DB4, LCM1602_IIC2.D4
  N31: LCD2.DB5, LCM1602_IIC2.D5
  N32: LCD2.DB6, LCM1602_IIC2.D6
  N33: LCD2.DB7, LCM1602_IIC2.D7
  N34: LCD2.LED+, LCM1602_IIC2.A
  N35: LCD2.LED-, LCM1602_IIC2.K
  N36: LCM1602_IIC2.LED_A, LCM1602_IIC2.LED_B
  N37: DHT1.DATA, R2.Pin_0
  N38: D2F1.NO, R3.Pin_0
  N39: D2F2.NO, R4.Pin_0
  GND_2: Driver2.GND, Power_plug2.GND
  N40: Driver2.Vmotor, Power_plug2.VCC
  N41: Driver2.blue-pin, SM2.blue-pin
  N42: Driver2.pink-pin, SM2.pink-pin
  N43: Driver2.yellow-pin, SM2.yellow-pin
  N44: Driver2.orange-pin, SM2.orange-pin
  N45: Driver2.red-pin, SM2.red-pin
  GND_3: Driver3.GND, Power_plug3.GND
  N46: Driver3.Vmotor, Power_plug3.VCC
  N47: Driver3.blue-pin, SM3.blue-pin
  N48: Driver3.pink-pin, SM3.pink-pin
  N49: Driver3.yellow-pin, SM3.yellow-pin
  N50: Driver3.orange-pin, SM3.orange-pin
  N51: Driver3.red-pin, SM3.red-pin
  N52: LED1.red_anode, R6.Pin_0
  N53: LED1.blue_anode, R7.Pin_0
  N54: LED1.green_anode, R8.Pin_0

custom parts:
  YL-83 Rain Sensor - Control Board: The YL-83 is a rain sensor that has more resistance when dry and less resistance when wet. The module runs at 5V.
  YL-83 Rain Sensor - Detection Board: The YL-83 is a rain sensor that has more resistance when dry and less resistance when wet. The module runs at 5V.
  LCM1602 IIC: I2C-Module to use a 1602 or 2004 LCD on with the wire.h libory Serial LCD Modul
  DHT11 Humitidy and Temperature Sensor: DHT11 Humidity and Temperature Sensor
  D2F-FL Omron Snap Action Limit Switch with Level: Snap action switch with stainless steel lever.
  28BYJ-48 Driver Module: High-power ULN2003 Stepper Motor Driver Board Test Module For Arduino AVR SMD
  28BYJ-48 Stepper Motor: Unipolar Stepper Motor 28BYJ-48 Top coil - pink & orange Bottom coil - blue & yellow Common rail - red Connector pins: blue - pink - yellow - orange - red
  Tower Pro SG90 servo: Original file by John De Cristofaro http://www.adafruit.com/products/1449 Adafruit Feedback Servo (Small) Edited by: e-radionica.com 28/9/2015
  MH-ET LIVE ESP32 DEVKIT 38 pins: http://mh.nodebb.com/topic/2/mh-et-live-esp32-devkit
