# Fritzing sketch Automated Window System Sketch v2_without ESP32  (saved by Fritzing 0.9.10b)

parts:
  Onderdeel3 = Arduino Uno (Rev3)
  S2 = Pushbutton [package=THT]
  C3 = Capacitor Polarized [package=panasonic_d]  # not connected
  C4 = Capacitor Polarized [package=panasonic_d]  # not connected
  R11 = Resistor [tolerance=±5% resistance=1.5k package="2512 [SMD]"]  # not connected
  R12 = Resistor [tolerance=±5% resistance=1.5k package="2512 [SMD]"]  # not connected
  LED2 = RGB LED (com. cathode, rbg) [package="5 mm [THT]"]
  R13 = Resistor [tolerance=±5% resistance=220 power=0.25 package=THT]
  R14 = Resistor [tolerance=±5% resistance=220 power=0.25 package=THT]
  R15 = Resistor [tolerance=±5% resistance=220 power=0.25 package=THT]
  PIR2 = PIR sensor
  Part5 = Infra red receiver
  D2F3 = D2F-FL Omron Snap Action Limit Switch with Level
  D2F4 = D2F-FL Omron Snap Action Limit Switch with Level
  R16 = Resistor [tolerance=±5% resistance=10k power=0.25 package=THT]
  R17 = Resistor [tolerance=±5% resistance=10k power=0.25 package=THT]
  SERVO3 = Tower Pro SG90 servo [part_number=101246]
  SERVO4 = Tower Pro SG90 servo [part_number=101246]
  DHT2 = DHT11 Humitidy and Temperature Sensor
  R18 = Resistor [tolerance=±5% resistance=10k package="0402 [SMD]"]
  J4 = Piezo Speaker
  Part6 = MQ-4
  LCD3 = LCD screen
  Part7 = MQ-4
  YL-83_-_Control_Board3 = YL-83 Rain Sensor - Control Board
  YL-83_-_Detection_Board3 = YL-83 Rain Sensor - Detection Board
  LCM1602_IIC3 = LCM1602 IIC [part_number="LCM1602 IIC" chip_label="LCM1602 IIC" package="DIP (Dual Inline) [THT]"]

nets:
  N1: Onderdeel3.A0, YL-83_-_Control_Board3.AO
  N2: Onderdeel3.A2, Part6.GND
  N3: Onderdeel3.A3, Part7.GND
  N4: Onderdeel3.A4/SDA, LCM1602_IIC3.SDA
  N5: Onderdeel3.A5/SCL, LCM1602_IIC3.SCL
  N6: Onderdeel3.D8, R18.Pin_1
  N7: Onderdeel3.D9_PWM, R13.Pin_1
  N8: Onderdeel3.D10_PWM/SS, R14.Pin_1
  N9: Onderdeel3.D11_PWM/MOSI, R15.Pin_1
  N10: Onderdeel3.D12/MISO, SERVO4.+5V
  GND: Onderdeel3.GND, LCM1602_IIC3.GND
  N11: Onderdeel3.D2, R16.Pin_1
  N12: Onderdeel3.D3_PWM, R17.Pin_1
  N13: Onderdeel3.D4, PIR2.SIG
  N14: Onderdeel3.D5_PWM, Part5.Data
  N15: Onderdeel3.D6_PWM, J4.pin2
  N16: Onderdeel3.D7, SERVO3.+5V
  N17: Onderdeel3.RESET, S2.leg0
  5V: Onderdeel3.5V, LCM1602_IIC3.VCC
  N18: LED2.red_anode, R15.Pin_0
  N19: LED2.blue_anode, R14.Pin_0
  N20: LED2.green_anode, R13.Pin_0
  N21: D2F3.NO, R16.Pin_0
  N22: D2F4.NO, R17.Pin_0
  N23: DHT2.DATA, R18.Pin_0
  VSS: LCD3.VSS, LCM1602_IIC3.VSS
  VDD: LCD3.VDD, LCM1602_IIC3.VDD
  N24: LCD3.V0, LCM1602_IIC3.V0
  N25: LCD3.RS, LCM1602_IIC3.RS
  N26: LCD3.R/W, LCM1602_IIC3.RW
  N27: LCD3.E, LCM1602_IIC3.E
  N28: LCD3.DB0, LCM1602_IIC3.D0
  N29: LCD3.DB1, LCM1602_IIC3.D1
  N30: LCD3.DB2, LCM1602_IIC3.D2
  N31: LCD3.DB3, LCM1602_IIC3.D3
  N32: LCD3.DB4, LCM1602_IIC3.D4
  N33: LCD3.DB5, LCM1602_IIC3.D5
  N34: LCD3.DB6, LCM1602_IIC3.D6
  N35: LCD3.DB7, LCM1602_IIC3.D7
  N36: LCD3.LED+, LCM1602_IIC3.A
  N37: LCD3.LED-, LCM1602_IIC3.K
  N38: YL-83_-_Control_Board3.POS, YL-83_-_Detection_Board3.POS
  N39: YL-83_-_Control_Board3.NEG, YL-83_-_Detection_Board3.NEG
  N40: LCM1602_IIC3.LED_A, LCM1602_IIC3.LED_B

custom parts:
  D2F-FL Omron Snap Action Limit Switch with Level: Snap action switch with stainless steel lever.
  Tower Pro SG90 servo: Original file by John De Cristofaro http://www.adafruit.com/products/1449 Adafruit Feedback Servo (Small) Edited by: e-radionica.com 28/9/2015
  DHT11 Humitidy and Temperature Sensor: DHT11 Humidity and Temperature Sensor
  YL-83 Rain Sensor - Control Board: The YL-83 is a rain sensor that has more resistance when dry and less resistance when wet. The module runs at 5V.
  YL-83 Rain Sensor - Detection Board: The YL-83 is a rain sensor that has more resistance when dry and less resistance when wet. The module runs at 5V.
  LCM1602 IIC: I2C-Module to use a 1602 or 2004 LCD on with the wire.h libory Serial LCD Modul
